# Fritzing sketch Excess Correlation Device (saved by Fritzing 0.9.3b)
breadboards: 1

parts:
  Bauteil1 = Arduino Uno (Rev3)
  Q1 = npn-Powertransistor [package="TO220 [THT]"]
  D1 = Diode [package=diode-1n4148]
  LED1 = LED - 3mm [color="Red (633nm)" package="3 mm [THT]"]
  R1 = Resistor [tolerance=±5% resistance=220 package=THT]

nets:
  N1: Bauteil1.D9_PWM, LED1.anode
  N2: Q1.base, R1.Pin_1
  N3: Q1.collector, D1.A
  N4: LED1.cathode, R1.Pin_0

notes:
  To Right Hand Side
  To Left Hand Side
